// Logisim project smips.circ as structural Verilog: 12 circuits, main circuit Board
module Board (
);

  wire CLK, HALT, MEM_WE, RESET, TTY_WE;
  wire [3:0] MEM_BE;
  wire [6:0] TTY_DATA;
  wire [31:0] MEM_ADDR, MEM_RDATA, MEM_WDATA;

  Clock Reloj (.out(CLK));
  Button u_Reset (.out(RESET));
  CPU cpu_1 (
    .CLK(CLK), .RESET(RESET), .MEM_RDATA(MEM_RDATA), .MEM_ADDR(MEM_ADDR), .MEM_WDATA(MEM_WDATA),
    .MEM_BE(MEM_BE), .MEM_WE(MEM_WE), .TTY_DATA(TTY_DATA), .TTY_WE(TTY_WE), .HALT(HALT));
  TTY #(.cols(48), .rows(12)) tty_1 (.data(TTY_DATA), .clk(CLK), .we(TTY_WE), .clr(RESET));
  Memory memory_1 (.CLK(CLK), .ADDR(MEM_ADDR), .WDATA(MEM_WDATA), .BE(MEM_BE), .WE(MEM_WE), .RDATA(MEM_RDATA));
  LED u_Halt (.in(HALT));

  // Notes on the sheet:
  //   S-MIPS | Board
  //   No modificar: la CPU se implementa dentro del subcircuito CPU.
endmodule

module CPU (
  input  CLK,
  input  RESET,
  input  [31:0] MEM_RDATA,
  output [31:0] MEM_ADDR,
  output [31:0] MEM_WDATA,
  output [3:0] MEM_BE,
  output MEM_WE,
  output [6:0] TTY_DATA,
  output TTY_WE,
  output HALT
);

  wire ALUSrcA, Branch_Enable, Branch_Taken, IRWrite, is_beq, is_bne, is_illegal, is_jr, is_lb, is_R, is_sb,
       is_store, is_syscall, MemtoReg, PCWrite, RegDst, RegWrite, zero;
  wire [1:0] ALUSrcB, ext_op, PCSrc;
  wire [2:0] alu_op, ALUOp;
  wire [3:0] instr_type;
  wire [5:0] funct, opcode;

  Branch_Control branch_control_1 (
    .zero(zero), .is_beq(is_beq), .is_bne(is_bne), .Branch_Enable(Branch_Enable), .Branch_Taken(Branch_Taken));
  Datapath datapath_1 (
    .clk(CLK), .reset(RESET), .MEM_RDATA(MEM_RDATA), .PCWrite(PCWrite), .IRWrite(IRWrite),
    .RegWrite(RegWrite), .ALUSrcA(ALUSrcA), .ALUSrcB(ALUSrcB), .ALUOp(ALUOp), .PCSrc(PCSrc),
    .MemtoReg(MemtoReg), .RegDst(RegDst), .ExtOp(ext_op), .StoreType(is_sb), .LoadType(is_lb),
    .MEM_WDATA(MEM_WDATA), .MEM_BE(MEM_BE), .MEM_ADDR(MEM_ADDR), .TTY_DATA(TTY_DATA), .opcode(opcode),
    .funct(funct), .Zero(zero));
  Instruction_Decoder instruction_decoder_1 (
    .opcode(opcode), .funct(funct), .alu_op(alu_op), .is_R(is_R), .is_jr(is_jr), .ext_op(ext_op),
    .is_beq(is_beq), .instr_type(instr_type), .is_bne(is_bne), .illegal(is_illegal), .is_sb(is_sb),
    .is_store(is_store), .is_lb(is_lb), .is_syscall(is_syscall));
  Control_Unit control_unit_1 (
    .is_R(is_R), .is_jr(is_jr), .clk(CLK), .reset(RESET), .instr_type(instr_type), .is_syscall(is_syscall),
    .Branch_Taken(Branch_Taken), .is_store(is_store), .alu_op(alu_op), .is_illegal(is_illegal),
    .PCWrite(PCWrite), .IRWrite(IRWrite), .RegWrite(RegWrite), .MemWrite(MEM_WE), .ALUSrcA(ALUSrcA),
    .ALUSrcB(ALUSrcB), .MemtoReg(MemtoReg), .ALUOp(ALUOp), .PCSrc(PCSrc), .RegDst(RegDst), .HALT(HALT),
    .TTY_WE(TTY_WE), .Branch_Enable(Branch_Enable));

  // Other names for the same wires on the sheet: MemWrite = MEM_WE

  // Notes on the sheet:
  //   CPU S-MIPS: implementar aqui
  //   No cambiar nombres, anchos ni sentido de los pines: la placa depende de ellos.
endmodule

module Memory (
  input  CLK,
  input  [31:0] ADDR,
  input  [31:0] WDATA,
  input  [3:0] BE,
  input  WE,
  output [31:0] RDATA
);

  RAM #(.addrWidth(12), .asyncread("true"), .byteenables("byteEnables"), .dataWidth(32), .\type ("nonvolatile")) Main_Memory (
    .addr(ADDR[13:2]), .we(WE), .oe(1'b1), .clk(CLK), .din(WDATA), .dout(RDATA), .be3(BE[3]), .be2(BE[2]),
    .be1(BE[1]), .be0(BE[0]));

  // Other names for the same wires on the sheet: A[11:0] = ADDR[13:2]

  // Notes on the sheet:
  //   Memoria unificada: 4096 palabras de 32 bits (16 KiB), little-endian
  //   Lectura combinacional; escritura en el flanco de subida de CLK con WE=1, solo en los bytes con BE=1.
  //   Se usan los bits 13..2 de ADDR; los demas se ignoran (el espacio se repite cada 16 KiB).
endmodule

module Datapath (
  input  clk,
  input  reset,
  input  [31:0] MEM_RDATA,
  input  PCWrite,
  input  IRWrite,
  input  RegWrite,
  input  ALUSrcA,
  input  [1:0] ALUSrcB,
  input  [2:0] ALUOp,
  input  [1:0] PCSrc,
  input  MemtoReg,
  input  RegDst,
  input  [1:0] ExtOp,
  input  StoreType,
  input  LoadType,
  output [31:0] MEM_WDATA,
  output [3:0] MEM_BE,
  output [31:0] MEM_ADDR,
  output [6:0] TTY_DATA,
  output [5:0] opcode,
  output [5:0] funct,
  output Zero
);

  wire [4:0] dir_rd, dir_rs, dir_rt, multiplexer_5_out;
  wire [10:6] IR_salida;
  wire [31:0] ALUOut, Dato_B, dato_extendido, inmediato_ext, jump, multiplexer_1_out, multiplexer_2_out,
       multiplexer_3_out, multiplexer_4_out, RD1, RD2, Result_ALU;
  wire [31:7] Dato_A;

  Multiplexer #(.width(32)) multiplexer_1 (
    .in0({Dato_A, TTY_DATA}), .in1(MEM_ADDR), .out(multiplexer_1_out), .sel(ALUSrcA));
  Multiplexer #(.select(2), .width(32)) multiplexer_2 (
    .in0(Dato_B), .in1(inmediato_ext), .in2(32'h4), .in3({32{1'b0}}), .out(multiplexer_2_out), .sel(ALUSrcB));
  Multiplexer #(.select(2), .width(32)) multiplexer_3 (
    .in0(ALUOut), .in1(jump), .in2({Dato_A, TTY_DATA}), .in3({32{1'b0}}), .out(multiplexer_3_out), .sel(PCSrc));
  ALU alu_1 (.A(multiplexer_1_out), .B(multiplexer_2_out), .ALU_Op(ALUOp), .Result(Result_ALU), .Zero(Zero));
  Register32 PC (.D(multiplexer_3_out), .WE(PCWrite), .clk(clk), .reset(reset), .salida(MEM_ADDR));
  Register32 A (.D(RD1), .WE(1'b1), .clk(clk), .reset(reset), .salida({Dato_A, TTY_DATA}));
  Register32 B (.D(RD2), .WE(1'b1), .clk(clk), .reset(reset), .salida(Dato_B));
  Memory_Interface memory_interface_1 (
    .MEM_RDATA(MEM_RDATA), .LoadType(LoadType), .MEM_ADDR(ALUOut[1:0]), .StoreType(StoreType),
    .Dato_B(Dato_B), .Dato_Extendido(dato_extendido), .MEM_BE(MEM_BE), .MEM_WDATA(MEM_WDATA));
  Multiplexer #(.width(32)) multiplexer_4 (.in0(dato_extendido), .in1(ALUOut), .out(multiplexer_4_out), .sel(MemtoReg));
  Multiplexer #(.width(5)) multiplexer_5 (.in0(dir_rt), .in1(dir_rd), .out(multiplexer_5_out), .sel(RegDst));
  Register_FIle register_file_1 (
    .WD(multiplexer_4_out), .WA(multiplexer_5_out), .RegWrite(RegWrite), .reset(reset), .clk(clk),
    .RA1(dir_rs), .RA2(dir_rt), .RD1(RD1), .RD2(RD2));
  Register32 IR (
    .D(MEM_RDATA), .WE(IRWrite), .clk(clk), .reset(reset),
    .salida({opcode, dir_rs, dir_rt, dir_rd, IR_salida, funct}));
  Register32 u_ALUOut (.D(Result_ALU), .WE(1'b1), .clk(clk), .reset(reset), .salida(ALUOut));
  Inmediate_Extender inmediate_extender_1 (.entrada({dir_rd, IR_salida, funct}), .ExtOp(ExtOp), .salida(inmediato_ext));

  // Other names for the same wires on the sheet: alu_op[2:0] = ALUOp; Dato_A[6:0] = TTY_DATA; ext_op[1:0] = ExtOp;
  //   load_type = LoadType; store_type = StoreType
endmodule

module Register_FIle (
  input  [31:0] WD,
  input  [4:0] WA,
  input  RegWrite,
  input  reset,
  input  clk,
  input  [4:0] RA1,
  input  [4:0] RA2,
  output [31:0] RD1,
  output [31:0] RD2
);

  wire L0, L1, L2, L3, L4, L5, L6, L7, L8, L9, L10, L11, L12, L13, L14, L15, L16, L17, L18, L19, L20, L21,
       L22, L23, L24, L25, L26, L27, L28, L29, L30, L31, S0, S1, S2, S3, S4, S5, S6, S7, S8, S9, S10, S11,
       S12, S13, S14, S15, S16, S17, S18, S19, S20, S21, S22, S23, S24, S25, S26, S27, S28, S29, S30, S31;
  wire [31:0] R0, R1, R2, R3, R4, R5, R6, R7, R8, R9, R10, R11, R12, R13, R14, R15, R16, R17, R18, R19, R20,
       R21, R22, R23, R24, R25, R26, R27, R28, R29, R30, R31;

  Decoder #(.enable("false"), .select(5)) decoder_1 (
    .out0(L0), .out1(L1), .out2(L2), .out3(L3), .out4(L4), .out5(L5), .out6(L6), .out7(L7), .out8(L8),
    .out9(L9), .out10(L10), .out11(L11), .out12(L12), .out13(L13), .out14(L14), .out15(L15), .out16(L16),
    .out17(L17), .out18(L18), .out19(L19), .out20(L20), .out21(L21), .out22(L22), .out23(L23), .out24(L24),
    .out25(L25), .out26(L26), .out27(L27), .out28(L28), .out29(L29), .out30(L30), .out31(L31), .sel(WA));
  and and_1 (S0, L0, RegWrite);
  and and_2 (S1, L1, RegWrite);
  and and_3 (S2, L2, RegWrite);
  and and_4 (S3, L3, RegWrite);
  and and_5 (S4, L4, RegWrite);
  and and_6 (S5, L5, RegWrite);
  and and_7 (S6, L6, RegWrite);
  and and_8 (S7, L7, RegWrite);
  and and_9 (S8, L8, RegWrite);
  and and_10 (S9, L9, RegWrite);
  and and_11 (S10, L10, RegWrite);
  and and_12 (S11, L11, RegWrite);
  and and_13 (S12, L12, RegWrite);
  and and_14 (S13, L13, RegWrite);
  and and_15 (S14, L14, RegWrite);
  and and_16 (S15, L15, RegWrite);
  and and_17 (S16, L16, RegWrite);
  and and_18 (S17, L17, RegWrite);
  and and_19 (S18, L18, RegWrite);
  and and_20 (S19, L19, RegWrite);
  and and_21 (S20, L20, RegWrite);
  and and_22 (S21, L21, RegWrite);
  and and_23 (S22, L22, RegWrite);
  and and_24 (S23, L23, RegWrite);
  and and_25 (S24, L24, RegWrite);
  and and_26 (S25, L25, RegWrite);
  and and_27 (S26, L26, RegWrite);
  and and_28 (S27, L27, RegWrite);
  and and_29 (S28, L28, RegWrite);
  and and_30 (S29, L29, RegWrite);
  and and_31 (S30, L30, RegWrite);
  and and_32 (S31, L31, RegWrite);
  Multiplexer #(.enable("true"), .select(5), .width(32)) multiplexer_1 (
    .in0(R0), .in1(R1), .in2(R2), .in3(R3), .in4(R4), .in5(R5), .in6(R6), .in7(R7), .in8(R8), .in9(R9),
    .in10(R10), .in11(R11), .in12(R12), .in13(R13), .in14(R14), .in15(R15), .in16(R16), .in17(R17),
    .in18(R18), .in19(R19), .in20(R20), .in21(R21), .in22(R22), .in23(R23), .in24(R24), .in25(R25),
    .in26(R26), .in27(R27), .in28(R28), .in29(R29), .in30(R30), .in31(R31), .out(RD2), .sel(RA2));  // open: en
  Register #(.width(32)) register_1 (.D(WD), .en(1'b0), .clk(clk), .Q(R0), .clr(reset));
  Register #(.width(32)) register_2 (.D(WD), .en(S1), .clk(clk), .Q(R1), .clr(reset));
  Register #(.width(32)) register_3 (.D(WD), .en(S2), .clk(clk), .Q(R2), .clr(reset));
  Register #(.width(32)) register_4 (.D(WD), .en(S3), .clk(clk), .Q(R3), .clr(reset));
  Register #(.width(32)) register_5 (.D(WD), .en(S4), .clk(clk), .Q(R4), .clr(reset));
  Register #(.width(32)) register_6 (.D(WD), .en(S5), .clk(clk), .Q(R5), .clr(reset));
  Register #(.width(32)) register_7 (.D(WD), .en(S6), .clk(clk), .Q(R6), .clr(reset));
  Register #(.width(32)) register_8 (.D(WD), .en(S7), .clk(clk), .Q(R7), .clr(reset));
  Register #(.width(32)) register_9 (.D(WD), .en(S8), .clk(clk), .Q(R8), .clr(reset));
  Register #(.width(32)) register_10 (.D(WD), .en(S9), .clk(clk), .Q(R9), .clr(reset));
  Register #(.width(32)) register_11 (.D(WD), .en(S10), .clk(clk), .Q(R10), .clr(reset));
  Register #(.width(32)) register_12 (.D(WD), .en(S11), .clk(clk), .Q(R11), .clr(reset));
  Register #(.width(32)) register_13 (.D(WD), .en(S12), .clk(clk), .Q(R12), .clr(reset));
  Register #(.width(32)) register_14 (.D(WD), .en(S13), .clk(clk), .Q(R13), .clr(reset));
  Register #(.width(32)) register_15 (.D(WD), .en(S14), .clk(clk), .Q(R14), .clr(reset));
  Register #(.width(32)) register_16 (.D(WD), .en(S15), .clk(clk), .Q(R15), .clr(reset));
  Register #(.width(32)) register_17 (.D(WD), .en(S16), .clk(clk), .Q(R16), .clr(reset));
  Register #(.width(32)) register_18 (.D(WD), .en(S17), .clk(clk), .Q(R17), .clr(reset));
  Register #(.width(32)) register_19 (.D(WD), .en(S18), .clk(clk), .Q(R18), .clr(reset));
  Register #(.width(32)) register_20 (.D(WD), .en(S19), .clk(clk), .Q(R19), .clr(reset));
  Register #(.width(32)) register_21 (.D(WD), .en(S20), .clk(clk), .Q(R20), .clr(reset));
  Register #(.width(32)) register_22 (.D(WD), .en(S21), .clk(clk), .Q(R21), .clr(reset));
  Register #(.width(32)) register_23 (.D(WD), .en(S22), .clk(clk), .Q(R22), .clr(reset));
  Register #(.width(32)) register_24 (.D(WD), .en(S23), .clk(clk), .Q(R23), .clr(reset));
  Register #(.width(32)) register_25 (.D(WD), .en(S24), .clk(clk), .Q(R24), .clr(reset));
  Register #(.width(32)) register_26 (.D(WD), .en(S25), .clk(clk), .Q(R25), .clr(reset));
  Register #(.width(32)) register_27 (.D(WD), .en(S26), .clk(clk), .Q(R26), .clr(reset));
  Register #(.width(32)) register_28 (.D(WD), .en(S27), .clk(clk), .Q(R27), .clr(reset));
  Register #(.width(32)) register_29 (.D(WD), .en(S28), .clk(clk), .Q(R28), .clr(reset));
  Register #(.width(32)) register_30 (.D(WD), .en(S29), .clk(clk), .Q(R29), .clr(reset));
  Register #(.width(32)) register_31 (.D(WD), .en(S30), .clk(clk), .Q(R30), .clr(reset));
  Register #(.width(32)) register_32 (.D(WD), .en(S31), .clk(clk), .Q(R31), .clr(reset));
  Multiplexer #(.enable("true"), .select(5), .width(32)) multiplexer_2 (
    .in0(R0), .in1(R1), .in2(R2), .in3(R3), .in4(R4), .in5(R5), .in6(R6), .in7(R7), .in8(R8), .in9(R9),
    .in10(R10), .in11(R11), .in12(R12), .in13(R13), .in14(R14), .in15(R15), .in16(R16), .in17(R17),
    .in18(R18), .in19(R19), .in20(R20), .in21(R21), .in22(R22), .in23(R23), .in24(R24), .in25(R25),
    .in26(R26), .in27(R27), .in28(R28), .in29(R29), .in30(R30), .in31(R31), .out(RD1), .sel(RA1));  // open: en
endmodule

module ALU (
  input  [31:0] A,
  input  [31:0] B,
  input  [2:0] ALU_Op,
  output [31:0] Result,
  output Zero
);

  wire comparator_1_lt;
  wire [31:0] add, \and , multiplexer_1_out, not_1_out, op_SLL, \or , shifter_1_out, SLR, SLT;

  assign not_1_out = ~B;  // NOT_Gate not_1, 32 bits wide
  assign \and  = A & B;  // AND_Gate and_1, 32 bits wide
  assign \or  = A | B;  // OR_Gate or_1, 32 bits wide
  Multiplexer #(.width(32)) multiplexer_1 (.in0(B), .in1(not_1_out), .out(multiplexer_1_out), .sel(ALU_Op[0]));
  Comparator #(.width(32)) comparator_1 (.a(A), .b(B), .lt(comparator_1_lt));  // open: gt, eq
  assign SLT = {{31{1'b0}}, comparator_1_lt};  // Bit_Extender bit_extender_1
  Shifter #(.width(32)) shifter_1 (.in(B), .\dist (A[4:0]), .out(shifter_1_out));
  Shifter #(.shift("lr"), .width(32)) shifter_2 (.in(B), .\dist (A[4:0]), .out(SLR));
  Adder #(.width(32)) adder_1 (.a(A), .b(multiplexer_1_out), .out(add), .cin(ALU_Op[0]));  // open: cout
  Multiplexer #(.select(3), .width(32)) multiplexer_2 (
    .in0(\and ), .in1(\or ), .in2(add), .in3(add), .in4(SLT), .in5(op_SLL), .in6(SLR), .in7({32{1'b0}}),
    .out(Result), .sel(ALU_Op));
  nor nor_1 (Zero, Result[0], Result[1], Result[2], Result[3], Result[4], Result[5], Result[6], Result[7], Result[8], Result[9], Result[10], Result[11], Result[12], Result[13], Result[14], Result[15], Result[16], Result[17], Result[18], Result[19], Result[20], Result[21], Result[22], Result[23], Result[24], Result[25], Result[26], Result[27], Result[28], Result[29], Result[30], Result[31]);
endmodule

module Branch_Control (
  input  zero,
  input  is_beq,
  input  is_bne,
  input  Branch_Enable,
  output Branch_Taken
);

  wire and_1_out, and_2_out, not_1_out, or_1_out;

  not not_1 (not_1_out, zero);
  and and_1 (and_1_out, zero, is_beq);
  and and_2 (and_2_out, not_1_out, is_bne);
  or or_1 (or_1_out, and_1_out, and_2_out);
  and and_3 (Branch_Taken, or_1_out, Branch_Enable);
endmodule

module Control_Unit (
  input  is_R,
  input  is_jr,
  input  clk,
  input  reset,
  input  [3:0] instr_type,
  input  is_syscall,
  input  Branch_Taken,
  input  is_store,
  input  [2:0] alu_op,
  input  is_illegal,
  output PCWrite,
  output IRWrite,
  output RegWrite,
  output MemWrite,
  output ALUSrcA,
  output [1:0] ALUSrcB,
  output MemtoReg,
  output [2:0] ALUOp,
  output [1:0] PCSrc,
  output RegDst,
  output HALT,
  output TTY_WE,
  output Branch_Enable
);

  wire and_1_out, and_2_out, and_3_out, and_4_out, and_5_out, EXECUTE, EXECUTE_IN, FETCH_IN, MEM_ADDR,
       MEM_ADDR_IN, multiplexer_1_out, not_1_out, not_2_out, WRITEBACK, WRITEBACK_IN;

  D_Flip_Flop FETCH (.D(multiplexer_1_out), .clk(clk), .Q(ALUSrcB[0]));  // open: Qn, preset, reset
  Multiplexer multiplexer_1 (.in0(FETCH_IN), .in1(1'b1), .out(multiplexer_1_out), .sel(reset));
  D_Flip_Flop DECODE (.D(ALUSrcB[0]), .clk(clk), .Q(Branch_Enable), .reset(reset));  // open: Qn, preset
  D_Flip_Flop u_EXECUTE (.D(EXECUTE_IN), .clk(clk), .Q(EXECUTE), .reset(reset));  // open: Qn, preset
  D_Flip_Flop u_MEM_ADDR (.D(MEM_ADDR_IN), .clk(clk), .Q(MEM_ADDR), .reset(reset));  // open: Qn, preset
  D_Flip_Flop u_WRITEBACK (.D(WRITEBACK), .clk(clk), .Q(WRITEBACK), .reset(reset));  // open: Qn, preset
  not not_1 (not_1_out, is_store);
  and and_1 (and_1_out, instr_type[3], Branch_Enable);
  and and_2 (and_2_out, Branch_Taken, Branch_Enable);
  and and_3 (and_3_out, is_syscall, Branch_Enable);
  and and_4 (and_4_out, instr_type[3], Branch_Enable);
  and and_5 (and_5_out, Branch_Enable, instr_type[3]);
  not not_2 (not_2_out, is_store);
  or or_1 (ALUSrcB[1], Branch_Enable, MEM_ADDR);
  and and_6 (MemtoReg, WRITEBACK, instr_type[1], not_1_out);
  or or_2 (PCSrc[0], Branch_Taken, is_jr);
  or or_3 (PCSrc[1], is_jr, and_1_out);
  or or_4 (PCWrite, Branch_Taken, and_5_out, ALUSrcB[0]);
  and and_7 (RegWrite, WRITEBACK, not_2_out);
  and and_8 (MemWrite, WRITEBACK, is_store);
  or or_5 (ALUSrcA, ALUSrcB[0], Branch_Enable);
  Multiplexer #(.width(3)) multiplexer_2 (.in0(alu_op), .in1(3'b010), .out(ALUOp), .sel(ALUSrcB[0]));
  or or_6 (FETCH_IN, WRITEBACK, and_2_out, and_3_out, and_4_out);
  or or_7 (HALT, is_illegal, is_syscall);
  and and_9 (EXECUTE_IN, instr_type[0], Branch_Enable);
  and and_10 (MEM_ADDR_IN, Branch_Enable, instr_type[1]);
  or or_8 (WRITEBACK_IN, EXECUTE, MEM_ADDR);

  assign IRWrite = ALUSrcB[0];
  assign RegDst = is_R;
  assign TTY_WE = is_syscall;

  // Other names for the same wires on the sheet: DECODE_IN = ALUSrcB[0]; FETCH = ALUSrcB[0]; DECODE = Branch_Enable;
  //   instr_type_0 = instr_type[0]; instr_type_1 = instr_type[1]; instr_type_2 = instr_type[2];
  //   instr_type_3 = instr_type[3]
endmodule

module Instruction_Decoder (
  input  [5:0] opcode,
  input  [5:0] funct,
  output [2:0] alu_op,
  output is_R,
  output is_jr,
  output [1:0] ext_op,
  output is_beq,
  output [3:0] instr_type,
  output is_bne,
  output illegal,
  output is_sb,
  output is_store,
  output is_lb,
  output is_syscall
);

  wire comparator_17_eq, comparator_18_eq, comparator_19_eq, comparator_20_eq, comparator_21_eq,
       comparator_22_eq, comparator_23_eq, comparator_24_eq, comparator_25_eq, comparator_26_eq, is_add,
       is_addi, is_addiu, is_addu, is_and, is_andi, is_j, is_jal, is_lbu, is_lw, is_or, is_ori, is_sll,
       is_slt, is_slti, is_srl, is_sub, is_sw, or_3_out;

  Comparator #(.width(6)) comparator_1 (.a(opcode), .b(6'b100011), .eq(is_lw));  // open: gt, lt
  Comparator #(.width(6)) comparator_2 (.a(opcode), .b(6'b101011), .eq(is_sw));  // open: gt, lt
  Comparator #(.width(6)) comparator_3 (.a(opcode), .b(6'b000100), .eq(is_beq));  // open: gt, lt
  Comparator #(.width(6)) comparator_4 (.a(opcode), .b(6'b000101), .eq(is_bne));  // open: gt, lt
  Comparator #(.width(6)) comparator_5 (.a(opcode), .b(6'b000010), .eq(is_j));  // open: gt, lt
  Comparator #(.width(6)) comparator_6 (.a(opcode), .b(6'b000011), .eq(is_jal));  // open: gt, lt
  Comparator #(.width(6)) comparator_7 (.a(opcode), .b(6'b001000), .eq(is_addi));  // open: gt, lt
  Comparator #(.width(6)) comparator_8 (.a(opcode), .b(6'b001001), .eq(is_addiu));  // open: gt, lt
  Comparator #(.width(6)) comparator_9 (.a(opcode), .b(6'b001010), .eq(is_slti));  // open: gt, lt
  Comparator #(.width(6)) comparator_10 (.a(opcode), .b(6'b001100), .eq(is_andi));  // open: gt, lt
  Comparator #(.width(6)) comparator_11 (.a(opcode), .b(6'b001101), .eq(is_ori));  // open: gt, lt
  Comparator #(.width(6)) comparator_12 (.a(opcode), .b(6'b001111), .eq(ext_op[1]));  // open: gt, lt
  Comparator #(.width(6)) comparator_13 (.a(opcode), .b(6'b100000), .eq(is_lb));  // open: gt, lt
  Comparator #(.width(6)) comparator_14 (.a(opcode), .b(6'b100100), .eq(is_lbu));  // open: gt, lt
  Comparator #(.width(6)) comparator_15 (.a(opcode), .b(6'b101000), .eq(is_sb));  // open: gt, lt
  Comparator #(.width(6)) comparator_16 (.a(opcode), .b({6{1'b0}}), .eq(is_R));  // open: gt, lt
  Comparator #(.width(6)) comparator_17 (.a(funct), .b(6'b100000), .eq(comparator_17_eq));  // open: gt, lt
  Comparator #(.width(6)) comparator_18 (.a(funct), .b(6'b100001), .eq(comparator_18_eq));  // open: gt, lt
  Comparator #(.width(6)) comparator_19 (.a(funct), .b(6'b100010), .eq(comparator_19_eq));  // open: gt, lt
  Comparator #(.width(6)) comparator_20 (.a(funct), .b(6'b100100), .eq(comparator_20_eq));  // open: gt, lt
  Comparator #(.width(6)) comparator_21 (.a(funct), .b(6'b100101), .eq(comparator_21_eq));  // open: gt, lt
  Comparator #(.width(6)) comparator_22 (.a(funct), .b(6'b101010), .eq(comparator_22_eq));  // open: gt, lt
  Comparator #(.width(6)) comparator_23 (.a(funct), .b({6{1'b0}}), .eq(comparator_23_eq));  // open: gt, lt
  Comparator #(.width(6)) comparator_24 (.a(funct), .b(6'b000010), .eq(comparator_24_eq));  // open: gt, lt
  Comparator #(.width(6)) comparator_25 (.a(funct), .b(6'b001000), .eq(comparator_25_eq));  // open: gt, lt
  Comparator #(.width(6)) comparator_26 (.a(funct), .b(6'b001100), .eq(comparator_26_eq));  // open: gt, lt
  and and_1 (is_add, is_R, comparator_17_eq);
  and and_2 (is_addu, is_R, comparator_18_eq);
  and and_3 (is_sub, is_R, comparator_19_eq);
  and and_4 (is_and, is_R, comparator_20_eq);
  and and_5 (is_or, is_R, comparator_21_eq);
  and and_6 (is_slt, is_R, comparator_22_eq);
  and and_7 (is_sll, is_R, comparator_23_eq);
  and and_8 (is_srl, is_R, comparator_24_eq);
  and and_9 (is_jr, is_R, comparator_25_eq);
  and and_10 (is_syscall, is_R, comparator_26_eq);
  or or_1 (alu_op[0], is_sll, is_ori, is_or, is_sub, is_beq, is_bne);
  or or_2 (alu_op[2], is_slt, is_slti, is_sll, is_srl);
  or or_3 (or_3_out, is_j, is_jal, is_addi, is_addiu, is_andi, is_lw, is_sw, is_beq, is_bne, is_ori, ext_op[1], is_lb, is_lbu, is_sb, is_slti, is_add, is_addu, is_sub, is_and, is_or, is_slt, is_sll, is_srl, is_jr, is_syscall);
  not not_1 (illegal, or_3_out);
  or or_4 (alu_op[1], is_addu, is_addi, is_addiu, is_sub, is_add, is_sb, is_srl, is_lw, is_sw, is_lb, is_lbu);
  or or_5 (ext_op[0], is_andi, is_ori);
  or or_6 (instr_type[1], is_lw, is_sw, is_lb, is_lbu, is_sb);
  or or_7 (instr_type[2], is_beq, is_bne);
  or or_8 (instr_type[3], is_jr, is_j, is_jal);
  or or_9 (instr_type[0], is_add, is_addu, is_sub, is_and, is_or, is_slt, is_sll, ext_op[1], is_ori, is_andi, is_slti, is_addiu, is_addi, is_srl);
  or or_10 (is_store, is_sw, is_sb);

  // Other names for the same wires on the sheet: alu_op_0 = alu_op[0]; alu_op_1 = alu_op[1]; alu_op_2 = alu_op[2];
  //   ext_op_0 = ext_op[0]; is_lui = ext_op[1]; instr_type_0 = instr_type[0]; instr_type_1 = instr_type[1];
  //   instr_type_2 = instr_type[2]; instr_type_3 = instr_type[3]
endmodule

module Register32 (
  input  [31:0] D,
  input  WE,
  input  clk,
  input  reset,
  output [31:0] salida
);

  Register #(.width(32)) register_1 (.D(D), .en(WE), .clk(clk), .Q(salida), .clr(reset));
endmodule

module Inmediate_Extender (
  input  [15:0] entrada,
  input  [1:0] ExtOp,
  output [31:0] salida
);

  wire [31:0] bit_extender_1_out, bit_extender_2_out;

  assign bit_extender_1_out = {{16{entrada[15]}}, entrada};  // Bit_Extender bit_extender_1
  assign bit_extender_2_out = {{16{1'b0}}, entrada};  // Bit_Extender bit_extender_2
  Multiplexer #(.select(2), .width(32)) multiplexer_1 (
    .in0(bit_extender_1_out), .in1(bit_extender_2_out), .in2({entrada, {16{1'b0}}}), .in3({32{1'b0}}),
    .out(salida), .sel(ExtOp));
endmodule

module Memory_Interface (
  input  [31:0] MEM_RDATA,
  input  LoadType,
  input  [1:0] MEM_ADDR,
  input  StoreType,
  input  [31:0] Dato_B,
  output [31:0] Dato_Extendido,
  output [3:0] MEM_BE,
  output [31:0] MEM_WDATA
);

  wire [3:0] decoder_1_out0;
  wire [7:0] multiplexer_1_out;
  wire [31:0] bit_extender_1_out, bit_extender_2_out, bit_extender_3_out, shifter_1_out;

  Decoder #(.select(2)) decoder_1 (
    .out0(decoder_1_out0[0]), .out1(decoder_1_out0[1]), .out2(decoder_1_out0[2]), .out3(decoder_1_out0[3]),
    .sel(MEM_ADDR));  // open: en
  Multiplexer #(.select(2), .width(8)) multiplexer_1 (
    .in0(MEM_RDATA[7:0]), .in1(MEM_RDATA[15:8]), .in2(MEM_RDATA[23:16]), .in3(MEM_RDATA[31:24]),
    .out(multiplexer_1_out), .sel(MEM_ADDR));
  assign bit_extender_1_out = {{24{1'b0}}, Dato_B[7:0]};  // Bit_Extender bit_extender_1
  assign bit_extender_2_out = {{24{1'b0}}, multiplexer_1_out};  // Bit_Extender bit_extender_2
  assign bit_extender_3_out = {{24{multiplexer_1_out[7]}}, multiplexer_1_out};  // Bit_Extender bit_extender_3
  Multiplexer #(.width(4)) multiplexer_2 (.in0(4'b1111), .in1(decoder_1_out0), .out(MEM_BE), .sel(StoreType));
  Multiplexer #(.width(32)) multiplexer_3 (
    .in0(bit_extender_2_out), .in1(bit_extender_3_out), .out(Dato_Extendido), .sel(LoadType));
  Multiplexer #(.width(32)) multiplexer_4 (.in0(Dato_B), .in1(shifter_1_out), .out(MEM_WDATA), .sel(StoreType));
  Shifter #(.width(32)) shifter_1 (.in(bit_extender_1_out), .\dist ({MEM_ADDR, 3'b000}), .out(shifter_1_out));

  // Other names for the same wires on the sheet: store_type = StoreType
endmodule
